// Digital circuit IF.dig as structural Verilog
module IF (
  input  clk,
  input  pw,
  input  rs,
  input  [31:0] ad,
  input  clr,
  output [31:0] ir,
  output [31:0] pc
);

  wire u_fb_pc_clear_inst;
  wire [31:0] instmem_d;

  fb_pc #(.applicationType("IVERILOG"), .iverilogOptions("-y /Users/zhangyibo/riscvdesign/RISCVFirebird/Pipeline/rtl\n-I /Users/zhangyibo/riscvdesign/RISCVFirebird/Pipeline/rtl"), .CodeFile("/Users/zhangyibo/riscvdesign/RISCVFirebird/Pipeline/rtl/fb_pc.v")) u_fb_pc (
    .pc_write(pw), .clk(clk), .pc_reset(rs), .new_address(ad), .pc_clear(clr), .out_address(pc),
    .clear_inst(u_fb_pc_clear_inst));
  ROM #(.AddrBits(10), .Bits(32)) instmem (.A(pc[9:0]), .sel(1'b1), .D(instmem_d));
  Multiplexer #(.Bits(32)) multiplexer_1 (.sel(u_fb_pc_clear_inst), .in_0(instmem_d), .in_1({32{1'b0}}), .out(ir));

  // Notes on the sheet:
  //   clk: pin 2
  //   pw: 用于在插入气泡的时候锁住pc, pin 1
  //   rs: 用于重置pc, pin 3
  //   ir: 输出是指令寄存器中取出的指令, pin 6
  //   ad: 输入的32位pc新地址
  //   来源包括：pc自增或是分支指令的目的地址, pin 4
  //   pc: pc寄存器的数值, pin 7
  //   clr: 用于jalr产生的一周期暂停, pin 5
  //   contents of instmem (hex, n*v repeats v):
  //   100413,3000493,3a00913,4200993,593,40002283,fe829ee3,40102283
  //   ,92ca63,122d963,40928533,a05463,a585b3,fff50513,ffbff06f,9585b3
  //   ,40b02123,fe7ff06f,d00593,40b02123,5200593,40b02123,4900593,40b02123
  //   ,5300593,40b02123,4300593,40b02123,2d00593,40b02123,5600593,40b02123
  //   ,d00593,40b02123,fc5ff06f
endmodule
