// Digital circuit firebird_single_design.dig as structural Verilog
module firebird_single_design (
  input  in_1,
  input  clk
);

  wire NU;
  wire [31:0] add_1_s, u_firebird_pc_out_address;

  firebird_pc #(.applicationType("IVERILOG"), .iverilogOptions("-y /Users/zhangyibo/riscvdesign/RISCVFirebird/SingleCycle/rtl/ -I /Users/zhangyibo/riscvdesign/RISCVFirebird/SingleCycle/rtl/"), .CodeFile("/Users/zhangyibo/riscvdesign/RISCVFirebird/SingleCycle/rtl/firebird_pc.v")) u_firebird_pc (
    .clk(clk), .pc_reset(in_1), .new_address(add_1_s), .out_address(u_firebird_pc_out_address));
  Add #(.Bits(32)) add_1 (.a(u_firebird_pc_out_address), .b(32'h4), .c_i(1'b0), .s(add_1_s), .c_o(NU));
  // also tied to GND on the sheet: NU

  // Other names for the same wires on the sheet: C = clk

  // Notes on the sheet:
  //   clk: Hz: 2
endmodule
